# Fritzing sketch sketch (saved by Fritzing 0.9.5d)
circuit board: 8.46667cm x 5.64444cm
perfboards: 1

parts:
  DHT1 = DHT11 Humitidy and Temperature Sensor
  LED1 = RGB LED (com. anode, rbg) [package="5 mm [THT]"]
  Squix1 = OLED 0.96" 128x64 I2C SSD1306
  Nano = Arduino Nano (Rev3.0) (ICSP)
  J1 = Screw terminal - 2 pins [package=THT]
  J2 = Screw terminal - 2 pins [package=THT]

nets (from the breadboard view):
  VDD: DHT1.VDD, Squix1.VCC, Nano.VIN, J1.pin1
  N1: DHT1.DATA, Nano.D8
  GND: DHT1.GND, LED1.common_anode, Squix1.GND, Nano.GND, J1.pin2
  N2: LED1.red_cathode, Nano.D3
  N3: LED1.blue_cathode, Nano.D5
  N4: LED1.green_cathode, Nano.D6
  N5: Squix1.SCL, Nano.A5
  N6: Squix1.SCA, Nano.A4
  N7: Nano.D11/MOSI, J2.pin2
  N8: Nano.D12/MISO, J2.pin1

custom parts:
  DHT11 Humitidy and Temperature Sensor: DHT11 Humidity and Temperature Sensor
